// Logisim project 1.circ as structural Verilog: 1 circuit, main circuit main
module main (
  input  A0,
  input  A1
);

  wire and_1_out, and_2_out, and_3_out, and_4_out, not_1_out, not_2_out;

  not not_1 (not_1_out, A0);
  not not_2 (not_2_out, A1);
  and and_1 (and_1_out, not_1_out, not_2_out);
  and and_2 (and_2_out, not_2_out, A0);
  and and_3 (and_3_out, not_1_out, A1);
  and and_4 (and_4_out, A1, A0);
  // Probe on and_1_out
  // Probe on and_2_out
  // Probe on and_3_out
  // Probe on and_4_out
endmodule
