// Logisim project 2multiplexer.circ as structural Verilog: 1 circuit, main circuit main
module main (
  input  in_1,
  input  in_2,
  input  in_3,
  input  [1:0] in_4,
  input  in_5,
  input  in_6
);

  wire multiplexer_1_out, multiplexer_2_out, multiplexer_3_out, multiplexer_4_out, xor_1_out;

  Multiplexer #(.enable("true"), .select(2)) multiplexer_1 (
    .in0(in_1), .in1(in_3), .in2(in_5), .in3(in_6), .out(multiplexer_1_out), .sel(in_4), .en(in_2));
  Multiplexer multiplexer_2 (.in0(in_3), .in1(in_1), .out(multiplexer_2_out), .sel(in_4[1]));
  Multiplexer multiplexer_3 (.in0(in_5), .in1(in_6), .out(multiplexer_3_out), .sel(in_4[1]));
  Multiplexer multiplexer_4 (.in0(multiplexer_2_out), .in1(multiplexer_3_out), .out(multiplexer_4_out), .sel(in_4[0]));
  // Probe on xor_1_out
  xor xor_1 (xor_1_out, multiplexer_1_out, multiplexer_4_out);
endmodule
