// Logisim project 3adder.circ as structural Verilog: 1 circuit, main circuit main
module main (
  input  in_1,
  input  [3:0] A,
  input  [3:0] S,
  input  [3:0] B
);

  wire adder_1_cout;

  Adder #(.width(4)) adder_1 (.a(A), .b(B), .out(S), .cin(in_1), .cout(adder_1_cout));
  // Probe on adder_1_cout
endmodule
