// Logisim project 6SyncSeqCirc.circ as structural Verilog: 1 circuit, main circuit main
module main (
  input  [7:0] in_1,
  output [7:0] out_2
);

  wire button_1_out, clock_1_out, undriven;
  wire [7:0] adder_1_out, multiplexer_1_out, not_1_out;

  assign not_1_out = ~in_1;  // NOT_Gate not_1, 8 bits wide
  Button #(.press("passive")) button_1 (.out(button_1_out));
  Multiplexer #(.width(8)) multiplexer_1 (.in0(in_1), .in1(not_1_out), .out(multiplexer_1_out), .sel(button_1_out));
  Clock clock_1 (.out(clock_1_out));
  Adder adder_1 (.a(out_2), .b(multiplexer_1_out), .out(adder_1_out), .cin(button_1_out));  // open: cout
  Register register_1 (.D(adder_1_out), .clk(clock_1_out), .Q(out_2), .clr(undriven));  // open: en
endmodule
