// Logisim project 6two.circ as structural Verilog: 1 circuit, main circuit main
module main (
  input  [7:0] in_1,
  output [7:0] out_2
);

  wire clock_1_out, undriven_2;
  wire [7:0] register_1_q, undriven;

  // NOT_Gate not_1 is placed but not wired
  Button #(.press("passive")) button_1 ();  // open: out
  Adder adder_1 (.a(register_1_q));  // open: b, out, cin, cout
  Register register_1 (.D(undriven), .clk(clock_1_out), .Q(register_1_q), .clr(undriven_2));  // open: en
  Clock clock_1 (.out(clock_1_out));
  Multiplexer #(.width(8)) multiplexer_1 ();  // open: in0, in1, out, sel
endmodule
