// Logisim project latches.circ as structural Verilog: 3 circuits, main circuit DLatch
module DLatch (
  input  D,
  input  CLK,
  output out_3
);

  wire and_1_out, and_2_out, nor_1_out, not_1_out;

  not not_1 (not_1_out, D);
  and and_1 (and_1_out, D, CLK);
  and and_2 (and_2_out, CLK, not_1_out);
  nor nor_1 (nor_1_out, and_1_out, out_3);
  nor nor_2 (out_3, nor_1_out, and_2_out);
endmodule

module DFlipFlop (
  input  Din,
  input  CLK,
  output Q
);

  wire dlatch_1_out_3;

  DLatch dlatch_1 (.D(Din), .CLK(CLK), .out_3(dlatch_1_out_3));
  DLatch dlatch_2 (.D(dlatch_1_out_3), .CLK(CLK), .out_3(Q));
endmodule

module FourBitRegister (
  input  [3:0] X,
  input  [3:0] Y,
  input  in_3
);

  DFlipFlop dflipflop_1 (.Din(X[0]), .CLK(in_3), .Q(Y[0]));
  DFlipFlop dflipflop_2 (.Din(X[1]), .CLK(in_3), .Q(Y[1]));
  DFlipFlop dflipflop_3 (.Din(X[2]), .CLK(in_3), .Q(Y[2]));
  DFlipFlop dflipflop_4 (.Din(X[3]), .CLK(in_3), .Q(Y[3]));
endmodule
