// Logisim project ripplecarrier.circ as structural Verilog: 1 circuit, main circuit main
module main (
  input  in_1,
  input  [3:0] A,
  input  [3:0] in_3,
  input  [3:0] B
);

  wire adder_1_cout, adder_2_cout, adder_3_cout, adder_4_cout;

  Adder #(.width(1)) adder_1 (.a(A[0]), .b(B[0]), .out(in_3[0]), .cin(in_1), .cout(adder_1_cout));
  Adder #(.width(1)) adder_2 (.a(A[1]), .b(B[1]), .out(in_3[1]), .cin(adder_1_cout), .cout(adder_2_cout));
  Adder #(.width(1)) adder_3 (.a(A[2]), .b(B[2]), .out(in_3[2]), .cin(adder_2_cout), .cout(adder_3_cout));
  Adder #(.width(1)) adder_4 (.a(A[3]), .b(B[3]), .out(in_3[3]), .cin(adder_3_cout), .cout(adder_4_cout));
  // Probe on adder_4_cout
endmodule
